# Fritzing sketch Схема 1 (saved by Fritzing 0.9.5d)
breadboards: 1

parts:
  MD03A1 = Dual VNH2SP30 Motor Driver [part_number=MXI508]
  VCC1 = 4 x AAA Battery Mount
  VCC2 = 4 x AAA Battery Mount
  J1 = Infrared Proximity Sensor
  U1 = Vibration Motor- ROB-08449 [package=vibe-motor-10mm]
  U2 = Vibration Motor- ROB-08449 [package=vibe-motor-10mm]
  Компонент1 = SparkFun ESP8266 Thing

nets:
  N1: MD03A1.1INa, Компонент1.GPIO2
  N2: MD03A1.1INb, Компонент1.GPIO12
  N3: MD03A1.GND, VCC2.+
  N4: MD03A1.+5V_(IN), VCC1.+, VCC2.-
  N5: MD03A1.2INb#142, Компонент1.GPIO13
  N6: MD03A1.2INb#143, Компонент1.GPIO14
  N7: MD03A1.OUT_1A, U2.+
  N8: MD03A1.OUT_1B, U2.-
  N9: MD03A1.OUT_2A, U1.+
  N10: MD03A1.OUT_2B, U1.-
  N11: VCC1.-, Компонент1.VCC
  GND: J1.GND, Компонент1.GND
  N12: J1.Vcc, Компонент1.9
